// Logisim project CRC.circ as structural Verilog: 3 circuits, main circuit CRC
module CRC (
  input  [7:0] \A被除数 ,
  input  [3:0] \B除数 ,
  output [10:0] \CRC校验码 
);

  wire [3:0] \除法子电路_1_new_index , \除法子电路_1_out_5 , \除法子电路_2_new_index , \除法子电路_2_out_5 , \除法子电路_3_new_index ,
       \除法子电路_3_out_5 , \除法子电路_4_new_index , \除法子电路_4_out_5 , \除法子电路_5_new_index , \除法子电路_5_out_5 ,
       \除法子电路_6_new_index , \除法子电路_6_out_5 , \除法子电路_7_new_index , \除法子电路_7_out_5 ;
  wire [10:0] bit_extender_1_out, shifter_1_out, \除法子电路_1_new_被除数 , \除法子电路_2_new_被除数 , \除法子电路_3_new_被除数 ,
       \除法子电路_4_new_被除数 , \除法子电路_5_new_被除数 , \除法子电路_6_new_被除数 , \除法子电路_7_new_被除数 , \除法子电路_8_new_被除数 ;

  assign bit_extender_1_out = {{3{1'b0}}, \A被除数 };  // Bit_Extender bit_extender_1
  Shifter #(.width(11)) shifter_1 (.in(bit_extender_1_out), .\dist (4'b0011), .out(shifter_1_out));
  \除法子电路  \u_除法子电路_1  (
    .\被除数 (shifter_1_out), .\除数 (\B除数 ), .index(4'b0111), .\new_被除数 (\除法子电路_1_new_被除数 ),
    .out_5(\除法子电路_1_out_5 ), .new_index(\除法子电路_1_new_index ));
  \除法子电路  \u_除法子电路_2  (
    .\被除数 (\除法子电路_4_new_被除数 ), .\除数 (\除法子电路_4_out_5 ), .index(\除法子电路_4_new_index ),
    .\new_被除数 (\除法子电路_2_new_被除数 ), .out_5(\除法子电路_2_out_5 ), .new_index(\除法子电路_2_new_index ));
  \除法子电路  \u_除法子电路_3  (
    .\被除数 (\除法子电路_2_new_被除数 ), .\除数 (\除法子电路_2_out_5 ), .index(\除法子电路_2_new_index ),
    .\new_被除数 (\除法子电路_3_new_被除数 ), .out_5(\除法子电路_3_out_5 ), .new_index(\除法子电路_3_new_index ));
  \除法子电路  \u_除法子电路_4  (
    .\被除数 (\除法子电路_1_new_被除数 ), .\除数 (\除法子电路_1_out_5 ), .index(\除法子电路_1_new_index ),
    .\new_被除数 (\除法子电路_4_new_被除数 ), .out_5(\除法子电路_4_out_5 ), .new_index(\除法子电路_4_new_index ));
  \除法子电路  \u_除法子电路_5  (
    .\被除数 (\除法子电路_3_new_被除数 ), .\除数 (\除法子电路_3_out_5 ), .index(\除法子电路_3_new_index ),
    .\new_被除数 (\除法子电路_5_new_被除数 ), .out_5(\除法子电路_5_out_5 ), .new_index(\除法子电路_5_new_index ));
  \除法子电路  \u_除法子电路_6  (
    .\被除数 (\除法子电路_5_new_被除数 ), .\除数 (\除法子电路_5_out_5 ), .index(\除法子电路_5_new_index ),
    .\new_被除数 (\除法子电路_6_new_被除数 ), .out_5(\除法子电路_6_out_5 ), .new_index(\除法子电路_6_new_index ));
  \除法子电路  \u_除法子电路_7  (
    .\被除数 (\除法子电路_6_new_被除数 ), .\除数 (\除法子电路_6_out_5 ), .index(\除法子电路_6_new_index ),
    .\new_被除数 (\除法子电路_7_new_被除数 ), .out_5(\除法子电路_7_out_5 ), .new_index(\除法子电路_7_new_index ));
  \除法子电路  \u_除法子电路_8  (
    .\被除数 (\除法子电路_7_new_被除数 ), .\除数 (\除法子电路_7_out_5 ), .index(\除法子电路_7_new_index ),
    .\new_被除数 (\除法子电路_8_new_被除数 ));  // open: out_5, new_index
  assign \CRC校验码  = shifter_1_out | \除法子电路_8_new_被除数 ;  // OR_Gate or_1, 11 bits wide

  // Notes on the sheet:
  //   index
endmodule

module \除法子电路  (
  input  [10:0] \被除数 ,
  input  [3:0] \除数 ,
  input  [3:0] index,
  output [10:0] \new_被除数 ,
  output [3:0] out_5,
  output [3:0] new_index
);

  wire [2:0] \n4_div_4电路_1_余数 ;
  wire [3:0] bit_extender_1_out, \余数 ;
  wire [10:0] and_1_out, bit_extender_2_out, bit_extender_3_out, not_1_out, shifter_1_out, shifter_2_out,
       shifter_3_out;

  Shifter #(.width(11), .shift("lr")) shifter_1 (.in(\被除数 ), .\dist (index), .out(shifter_1_out));
  Bit_Extender #(.in_width(11), .out_width(4)) bit_extender_1 (.in(shifter_1_out), .out(bit_extender_1_out));
  \_4_div_4电路  \u_4_div_4电路_1  (.A(bit_extender_1_out), .B(\除数 ), .\余数 (\n4_div_4电路_1_余数 ));  // open: out_3
  assign bit_extender_2_out = {{7{1'b0}}, 4'b1111};  // Bit_Extender bit_extender_2
  assign bit_extender_3_out = {{7{1'b0}}, \余数 };  // Bit_Extender bit_extender_3
  assign \余数  = {{1{1'b0}}, \n4_div_4电路_1_余数 };  // Bit_Extender bit_extender_4
  Shifter #(.width(11)) shifter_2 (.in(bit_extender_2_out), .\dist (index), .out(shifter_2_out));
  assign not_1_out = ~shifter_2_out;  // NOT_Gate not_1, 11 bits wide
  Shifter #(.width(11)) shifter_3 (.in(bit_extender_3_out), .\dist (index), .out(shifter_3_out));
  assign and_1_out = \被除数  & not_1_out;  // AND_Gate and_1, 11 bits wide
  assign \new_被除数  = and_1_out | shifter_3_out;  // OR_Gate or_1, 11 bits wide
  Subtractor #(.width(4)) subtractor_1 (.a(index), .b(4'b0001), .out(new_index));  // open: bin, bout

  assign out_5 = \除数 ;

  // Other names for the same wires on the sheet: A[10:0] = \被除数 ; B[3:0] = \除数 
endmodule

module \_4_div_4电路  (
  input  [3:0] A,
  input  [3:0] B,
  output out_3,
  output [2:0] \余数 
);

  wire [3:0] multiplexer_1_out, xor_1_out;

  assign xor_1_out = A ^ B;  // XOR_Gate xor_1, 4 bits wide
  Multiplexer #(.width(4)) multiplexer_1 (.in0(A), .in1(xor_1_out), .out(multiplexer_1_out), .sel(A[3]));  // open: en
  Bit_Extender #(.in_width(4), .out_width(3)) bit_extender_1 (.in(multiplexer_1_out), .out(\余数 ));

  assign out_3 = A[3];

  // Other names for the same wires on the sheet: 商 = A[3]
endmodule
