// Logisim project CRC_0.circ as structural Verilog: 2 circuits, main circuit main
module main (
  input  [7:0] \A被除数 ,
  input  [3:0] \B除数 ,
  output [10:0] \CRC校验码 
);

  wire \四位除四位电路_1_商 ;
  wire [2:0] \四位除四位电路_1_余数 ;
  wire [3:0] undriven;

  \四位除四位电路  \u_四位除四位电路_1  (.\被除数 (undriven), .\除数 (\B除数 ), .\余数 (\四位除四位电路_1_余数 ), .\商 (\四位除四位电路_1_商 ));

  // Other names for the same wires on the sheet: 除数[3:0] = \B除数 

  // Notes on the sheet:
  //   太麻烦了，丢弃
endmodule

module \四位除四位电路  (
  input  [3:0] \被除数 ,
  input  [3:0] \除数 ,
  output [2:0] \余数 ,
  output \商 
);
endmodule
