// Logisim project fsm.circ as structural Verilog: 5 circuits, main circuit fsm
module fsm (
  input  [1:0] in_1,
  input  in_2,
  output out_3
);

  wire clk;
  wire [1:0] multiplexer_1_out, \状态存储_1_out_4 , \状态转移_1_out_3 ;

  Clock clock_1 (.out(clk));
  \状态转移  \u_状态转移_1  (.in_1(\状态存储_1_out_4 ), .in_2(in_1), .out_3(\状态转移_1_out_3 ));
  Multiplexer #(.width(2)) multiplexer_1 (
    .in0(\状态转移_1_out_3 ), .in1(2'b00), .out(multiplexer_1_out), .sel(in_2));  // open: en
  // Probe on multiplexer_1_out
  \状态存储  \u_状态存储_1  (.in_1(multiplexer_1_out), .in_2(clk), .in_3(in_2), .out_4(\状态存储_1_out_4 ));
  // Probe on \状态存储_1_out_4 
  \输出电路  \u_输出电路_1  (.in_1(\状态存储_1_out_4 ), .in_2(in_1), .out_3(out_3));

  // Other names for the same wires on the sheet: CLR = in_2; input[1:0] = in_1; output = out_3

  // Notes on the sheet:
  //   异步复位
endmodule

// state
module \状态转移  (
  input  [1:0] in_1,
  input  [1:0] in_2,
  output [1:0] out_3
);

  wire and_1_out, and_2_out, and_3_out, and_4_out, not_1_out, not_2_out, not_3_out, not_4_out, not_5_out,
       not_6_out, not_7_out;

  not not_1 (not_1_out, in_1[1]);
  not not_2 (not_2_out, in_2[0]);
  not not_3 (not_3_out, in_1[0]);
  not not_4 (not_4_out, in_2[0]);
  not not_5 (not_5_out, in_2[1]);
  not not_6 (not_6_out, in_1[0]);
  not not_7 (not_7_out, in_2[0]);
  and and_1 (and_1_out, not_1_out, in_1[0], not_2_out);
  and and_2 (and_2_out, in_1[1], not_3_out, not_4_out);
  and and_3 (and_3_out, not_5_out, in_2[0]);
  and and_4 (and_4_out, in_1[1], not_6_out, not_7_out);
  or or_1 (out_3[1], and_1_out, and_2_out);
  or or_2 (out_3[0], and_3_out, and_4_out);

  // Other names for the same wires on the sheet: in_0 = in_2[0]; input[1:0] = in_2; in_1_t = in_2[1];
  //   next_state[1:0] = out_3; out_0 = out_3[0]; out_1 = out_3[1]; s0 = in_1[0]; state[1:0] = in_1; s1 = in_1[1]
endmodule

// store
module \状态存储  (
  input  [1:0] in_1,
  input  in_2,
  input  in_3,
  output [1:0] out_4
);

  wire [1:0] register_2_q;

  Register #(.width(2)) register_1 (.D(in_1), .Q(out_4), .clk(in_2));  // open: en, clr
  Register #(.width(2)) register_2 (.Q(register_2_q), .clk(in_2), .clr(in_3));  // open: D, en

  // Other names for the same wires on the sheet: clk = in_2; CLR = in_3; input[1:0] = in_1; output[1:0] = out_4
endmodule

// output
module \输出电路  (
  input  [1:0] in_1,
  input  [1:0] in_2,
  output out_3
);

  wire not_1_out, not_2_out;

  not not_1 (not_1_out, in_1[0]);
  not not_2 (not_2_out, in_2[0]);
  and and_1 (out_3, in_1[1], not_1_out, not_2_out);

  // Other names for the same wires on the sheet: in_0 = in_2[0]; input[1:0] = in_2; in_1_t = in_2[1]; output = out_3;
  //   s0 = in_1[0]; state[1:0] = in_1; s1 = in_1[1]
endmodule

module temp (
  input  s1,
  input  s0,
  input  in_1,
  input  in_0,
  output \output 
);

  wire clock_1_out, CLR, not_1_out, not_2_out, register_1_q;

  and and_1 (\output , s1, not_1_out, not_2_out);
  not not_1 (not_1_out, s0);
  not not_2 (not_2_out, in_0);
  Register #(.width(1)) register_1 (.D(CLR), .Q(register_1_q), .clk(clock_1_out));  // open: en, clr
  Clock clock_1 (.out(clock_1_out));
  and and_2 (CLR, CLR, register_1_q);
endmodule
