// Logisim project ftoi.circ as structural Verilog: 6 circuits, main circuit ftoi
module ftoi (
  input  [15:0] in_1,
  output [31:0] out_2
);

  wire flag;
  wire [1:0] priority_encoder_1_out;
  wire [3:0] state;
  wire [4:0] E;
  wire [31:0] multiplexer_1_out, multiplexer_2_out, val, \负数补码_1_out_2 ;

  state state_1 (.in_1(in_1[14:10]), .out_2(state));
  calculate_E calculate_e_1 (.in_1(in_1[14:10]), .out_2(E));
  Normalized___Denormalized normalized_denormalized_1 (.in_1(in_1[9:0]), .in_2(E), .in_3(state), .out_4(val));
  \负数补码  \u_负数补码_1  (.in_1(val), .out_2(\负数补码_1_out_2 ));
  Comparator #(.width(5), .mode("unsigned")) comparator_1 (.a(in_1[14:10]), .b(5'b01111), .lt(flag));  // open: gt, eq
  Multiplexer #(.width(32)) multiplexer_1 (
    .in0(val), .in1(\负数补码_1_out_2 ), .out(multiplexer_1_out), .sel(in_1[15]));  // open: en
  Priority_Encoder #(.select(2)) priority_encoder_1 (
    .in0(state[0]), .in1(state[1]), .in2(state[2]), .in3(state[3]), .out(priority_encoder_1_out));  // open: gs, en_out, en_in
  Multiplexer #(.select(2), .width(32)) multiplexer_2 (
    .in0(multiplexer_1_out), .in1(multiplexer_1_out), .in2({32{1'b0}}), .out(multiplexer_2_out),
    .sel(priority_encoder_1_out));  // open: in3, en
  // Probe on priority_encoder_1_out
  Multiplexer #(.width(32)) multiplexer_3 (
    .in0(multiplexer_2_out), .in1({32{1'b0}}), .out(out_2), .sel(flag));  // open: en

  // Other names for the same wires on the sheet: float[15:0] = in_1; frac[9:0] = in_1[9:0]; exp[4:0] = in_1[14:10];
  //   sign = in_1[15]; int[31:0] = out_2

  // Notes on the sheet:
  //   正数
  //   增加flag进行特判
endmodule

module state (
  input  [4:0] in_1,
  output [3:0] out_2
);

  wire comparator_1_eq, comparator_2_eq, comparator_3_eq, comparator_4_eq, not_1_out, or_1_out;
  wire [3:0] bit_extender_1_out, bit_extender_2_out, bit_extender_3_out, shifter_1_out, shifter_2_out,
       shifter_3_out;

  // Probe on {5{1'b1}}
  // Probe on {5{1'b1}}
  Comparator #(.width(5), .mode("unsigned")) comparator_1 (
    .a(in_1), .b({5{1'b0}}), .eq(comparator_1_eq));  // open: gt, lt
  Comparator #(.width(5), .mode("unsigned")) comparator_2 (
    .a(in_1), .b({5{1'b1}}), .eq(comparator_2_eq));  // open: gt, lt
  Comparator #(.width(5), .mode("unsigned")) comparator_3 (
    .a(in_1), .b({5{1'b0}}), .eq(comparator_3_eq));  // open: gt, lt
  Comparator #(.width(5), .mode("unsigned")) comparator_4 (
    .a(in_1), .b({5{1'b1}}), .eq(comparator_4_eq));  // open: gt, lt
  or or_1 (or_1_out, comparator_1_eq, comparator_2_eq);
  not not_1 (not_1_out, or_1_out);
  assign bit_extender_1_out = {{3{1'b0}}, comparator_3_eq};  // Bit_Extender bit_extender_1
  assign bit_extender_2_out = {{3{1'b0}}, comparator_4_eq};  // Bit_Extender bit_extender_2
  assign bit_extender_3_out = {{3{1'b0}}, not_1_out};  // Bit_Extender bit_extender_3
  Shifter #(.width(4)) shifter_1 (.in(bit_extender_1_out), .\dist (2'b01), .out(shifter_1_out));
  Shifter #(.width(4)) shifter_2 (.in(bit_extender_2_out), .\dist (2'b10), .out(shifter_2_out));
  Shifter #(.width(4)) shifter_3 (.in(bit_extender_3_out), .\dist (2'b00), .out(shifter_3_out));
  // Probe on out_2
  ExactlyOne xor_1[3:0] (.out(out_2), .in0(shifter_3_out), .in2(shifter_1_out), .in4(shifter_2_out));

  // Other names for the same wires on the sheet: exp[4:0] = in_1; state[3:0] = out_2

  // Notes on the sheet:
  //   没用，为了直观
  //   Normalized
  //   Denormalized
  //   Infinity & NaN
  //   独热码
endmodule

// E
module calculate_E (
  input  [4:0] in_1,
  output [4:0] out_2
);

  // Probe on 5'b01111
  Subtractor #(.width(5)) subtractor_1 (.a(in_1), .b(5'b01111), .out(out_2));  // open: bin, bout

  // Other names for the same wires on the sheet: E[4:0] = out_2; exp[4:0] = in_1
endmodule

module Normalized (
  input  [9:0] in_1,
  input  [4:0] in_2,
  output [31:0] out_3
);

  wire [31:0] bit_extender_1_out, frac_int, shifter_1_out;

  assign bit_extender_1_out = {{22{1'b0}}, in_1};  // Bit_Extender bit_extender_1
  // Probe on 32'h400
  Shifter #(.width(32)) shifter_1 (.in(frac_int), .\dist (in_2), .out(shifter_1_out));
  assign frac_int = 32'h400 ^ bit_extender_1_out;  // XOR_Gate xor_1, 32 bits wide
  Shifter #(.width(32), .shift("lr")) shifter_2 (.in(shifter_1_out), .\dist (5'b01010), .out(out_3));
  // Probe on out_3

  // Other names for the same wires on the sheet: E[4:0] = in_2; frac[9:0] = in_1; val[31:0] = out_3
endmodule

// N&DN
module Normalized___Denormalized (
  input  [9:0] in_1,
  input  [4:0] in_2,
  input  [3:0] in_3,
  output [31:0] out_4
);

  wire [31:0] bit_extender_1_out, frac_int, multiplexer_1_out, shifter_1_out;

  assign bit_extender_1_out = {{22{1'b0}}, in_1};  // Bit_Extender bit_extender_1
  Multiplexer #(.width(32)) multiplexer_1 (
    .in0({32{1'b0}}), .in1(32'h400), .out(multiplexer_1_out), .sel(in_3[0]));  // open: en
  Shifter #(.width(32)) shifter_1 (.in(frac_int), .\dist (in_2), .out(shifter_1_out));
  assign frac_int = multiplexer_1_out ^ bit_extender_1_out;  // XOR_Gate xor_1, 32 bits wide
  Shifter #(.width(32), .shift("lr")) shifter_2 (.in(shifter_1_out), .\dist (5'b01010), .out(out_4));
  // Probe on out_4

  // Other names for the same wires on the sheet: E[4:0] = in_2; frac[9:0] = in_1; slect = in_3[0]; state[3:0] = in_3;
  //   val[31:0] = out_4
endmodule

// 负补
module \负数补码  (
  input  [31:0] in_1,
  output [31:0] out_2
);

  wire [31:0] not_1_out;

  assign not_1_out = ~in_1;  // NOT_Gate not_1, 32 bits wide
  Adder #(.width(32)) adder_1 (.a(not_1_out), .b(32'h1), .out(out_2));  // open: cin, cout
endmodule
