// Logisim project grf.circ as structural Verilog: 1 circuit, main circuit grf
module grf (
  input  in_1,
  input  in_2,
  input  in_3,
  input  [4:0] in_4,
  input  [4:0] in_5,
  input  [4:0] in_6,
  input  [31:0] in_7,
  output [31:0] out_8,
  output [31:0] out_9
);

  wire en_0, en_1, en_2, en_3, en_4, en_5, en_6, en_7, en_8, en_9, en_10, en_11, en_12, en_13, en_14, en_15,
       en_16, en_17, en_18, en_19, en_20, en_21, en_22, en_23, en_24, en_25, en_26, en_27, en_28, en_29,
       en_30, en_31, multiplexer_1_out;
  wire [31:0] Out_0, Out_1, Out_2, Out_3, Out_4, Out_5, Out_6, Out_7, Out_8_t, Out_9_t, Out_10, Out_11,
       Out_12, Out_13, Out_14, Out_15, Out_16, Out_17, Out_18, Out_19, Out_20, Out_21, Out_22, Out_23,
       Out_24, Out_25, Out_26, Out_27, Out_28, Out_29, Out_30, Out_31;

  Demultiplexer #(.select(5)) demultiplexer_1 (
    .out0(en_0), .out1(en_1), .out2(en_2), .out3(en_3), .out4(en_4), .out5(en_5), .out6(en_6), .out7(en_7),
    .out8(en_8), .out9(en_9), .out10(en_10), .out11(en_11), .out12(en_12), .out13(en_13), .out14(en_14),
    .out15(en_15), .out16(en_16), .out17(en_17), .out18(en_18), .out19(en_19), .out20(en_20), .out21(en_21),
    .out22(en_22), .out23(en_23), .out24(en_24), .out25(en_25), .out26(en_26), .out27(en_27), .out28(en_28),
    .out29(en_29), .out30(en_30), .out31(en_31), .in(multiplexer_1_out), .sel(in_6));  // open: en
  Multiplexer multiplexer_1 (.in0(1'b0), .in1(1'b1), .out(multiplexer_1_out), .sel(in_3));  // open: en
  Multiplexer #(.select(5), .width(32)) multiplexer_2 (
    .in0(Out_0), .in1(Out_1), .in2(Out_2), .in3(Out_3), .in4(Out_4), .in5(Out_5), .in6(Out_6), .in7(Out_7),
    .in8(Out_8_t), .in9(Out_9_t), .in10(Out_10), .in11(Out_11), .in12(Out_12), .in13(Out_13), .in14(Out_14),
    .in15(Out_15), .in16(Out_16), .in17(Out_17), .in18(Out_18), .in19(Out_19), .in20(Out_20), .in21(Out_21),
    .in22(Out_22), .in23(Out_23), .in24(Out_24), .in25(Out_25), .in26(Out_26), .in27(Out_27), .in28(Out_28),
    .in29(Out_29), .in30(Out_30), .in31(Out_31), .out(out_8), .sel(in_4));  // open: en
  Multiplexer #(.select(5), .width(32)) multiplexer_3 (
    .in0(Out_0), .in1(Out_1), .in2(Out_2), .in3(Out_3), .in4(Out_4), .in5(Out_5), .in6(Out_6), .in7(Out_7),
    .in8(Out_8_t), .in9(Out_9_t), .in10(Out_10), .in11(Out_11), .in12(Out_12), .in13(Out_13), .in14(Out_14),
    .in15(Out_15), .in16(Out_16), .in17(Out_17), .in18(Out_18), .in19(Out_19), .in20(Out_20), .in21(Out_21),
    .in22(Out_22), .in23(Out_23), .in24(Out_24), .in25(Out_25), .in26(Out_26), .in27(Out_27), .in28(Out_28),
    .in29(Out_29), .in30(Out_30), .in31(Out_31), .out(out_9), .sel(in_5));  // open: en
  Register #(.width(32)) register_1 (.D(in_7), .en(1'b0), .Q(Out_0), .clk(in_1), .clr(in_2));
  Register #(.width(32)) register_2 (.D(in_7), .en(en_4), .Q(Out_4), .clk(in_1), .clr(in_2));
  Register #(.width(32)) register_3 (.D(in_7), .en(en_8), .Q(Out_8_t), .clk(in_1), .clr(in_2));
  Register #(.width(32)) register_4 (.D(in_7), .en(en_12), .Q(Out_12), .clk(in_1), .clr(in_2));
  Register #(.width(32)) register_5 (.D(in_7), .en(en_16), .Q(Out_16), .clk(in_1), .clr(in_2));
  Register #(.width(32)) register_6 (.D(in_7), .en(en_20), .Q(Out_20), .clk(in_1), .clr(in_2));
  Register #(.width(32)) register_7 (.D(in_7), .en(en_24), .Q(Out_24), .clk(in_1), .clr(in_2));
  Register #(.width(32)) register_8 (.D(in_7), .en(en_28), .Q(Out_28), .clk(in_1), .clr(in_2));
  Register #(.width(32)) register_9 (.D(in_7), .en(en_1), .Q(Out_1), .clk(in_1), .clr(in_2));
  Register #(.width(32)) register_10 (.D(in_7), .en(en_5), .Q(Out_5), .clk(in_1), .clr(in_2));
  Register #(.width(32)) register_11 (.D(in_7), .en(en_9), .Q(Out_9_t), .clk(in_1), .clr(in_2));
  Register #(.width(32)) register_12 (.D(in_7), .en(en_13), .Q(Out_13), .clk(in_1), .clr(in_2));
  Register #(.width(32)) register_13 (.D(in_7), .en(en_17), .Q(Out_17), .clk(in_1), .clr(in_2));
  Register #(.width(32)) register_14 (.D(in_7), .en(en_21), .Q(Out_21), .clk(in_1), .clr(in_2));
  Register #(.width(32)) register_15 (.D(in_7), .en(en_25), .Q(Out_25), .clk(in_1), .clr(in_2));
  Register #(.width(32)) register_16 (.D(in_7), .en(en_29), .Q(Out_29), .clk(in_1), .clr(in_2));
  Register #(.width(32)) register_17 (.D(in_7), .en(en_2), .Q(Out_2), .clk(in_1), .clr(in_2));
  Register #(.width(32)) register_18 (.D(in_7), .en(en_6), .Q(Out_6), .clk(in_1), .clr(in_2));
  Register #(.width(32)) register_19 (.D(in_7), .en(en_10), .Q(Out_10), .clk(in_1), .clr(in_2));
  Register #(.width(32)) register_20 (.D(in_7), .en(en_14), .Q(Out_14), .clk(in_1), .clr(in_2));
  Register #(.width(32)) register_21 (.D(in_7), .en(en_18), .Q(Out_18), .clk(in_1), .clr(in_2));
  Register #(.width(32)) register_22 (.D(in_7), .en(en_22), .Q(Out_22), .clk(in_1), .clr(in_2));
  Register #(.width(32)) register_23 (.D(in_7), .en(en_26), .Q(Out_26), .clk(in_1), .clr(in_2));
  Register #(.width(32)) register_24 (.D(in_7), .en(en_30), .Q(Out_30), .clk(in_1), .clr(in_2));
  Register #(.width(32)) register_25 (.D(in_7), .en(en_3), .Q(Out_3), .clk(in_1), .clr(in_2));
  Register #(.width(32)) register_26 (.D(in_7), .en(en_7), .Q(Out_7), .clk(in_1), .clr(in_2));
  Register #(.width(32)) register_27 (.D(in_7), .en(en_11), .Q(Out_11), .clk(in_1), .clr(in_2));
  Register #(.width(32)) register_28 (.D(in_7), .en(en_15), .Q(Out_15), .clk(in_1), .clr(in_2));
  Register #(.width(32)) register_29 (.D(in_7), .en(en_19), .Q(Out_19), .clk(in_1), .clr(in_2));
  Register #(.width(32)) register_30 (.D(in_7), .en(en_23), .Q(Out_23), .clk(in_1), .clr(in_2));
  Register #(.width(32)) register_31 (.D(in_7), .en(en_27), .Q(Out_27), .clk(in_1), .clr(in_2));
  Register #(.width(32)) register_32 (.D(in_7), .en(en_31), .Q(Out_31), .clk(in_1), .clr(in_2));

  // Other names for the same wires on the sheet: A1[4:0] = in_4; A2[4:0] = in_5; A3[4:0] = in_6; clk = in_1;
  //   RD1[31:0] = out_8; RD2[31:0] = out_9; rst = in_2; In[31:0] = in_7; WD[31:0] = in_7; WE = in_3
endmodule
