// Logisim project mealy_navigation.circ as structural Verilog: 5 circuits, main circuit navigation
module navigation (
  input  [1:0] in_1,
  input  in_2,
  input  in_3,
  output out_4,
  output out_5
);

  wire \输出电路_1_out_3 , \输出电路_1_out_4 ;
  wire [2:0] \状态存储_1_out_4 , \状态转移_1_out_3 ;

  // Probe on in_1
  \状态转移  \u_状态转移_1  (.in_1(in_1), .in_2(\状态存储_1_out_4 ), .out_3(\状态转移_1_out_3 ));
  // Probe on \状态存储_1_out_4 
  // Probe on \状态转移_1_out_3 
  \状态存储  \u_状态存储_1  (.in_1(\状态转移_1_out_3 ), .in_2(in_2), .in_3(in_3), .out_4(\状态存储_1_out_4 ));
  \输出电路  \u_输出电路_1  (.in_1(in_1), .in_2(\状态存储_1_out_4 ), .out_3(\输出电路_1_out_3 ), .out_4(\输出电路_1_out_4 ));
  Register #(.width(1)) register_1 (.D(\输出电路_1_out_3 ), .Q(out_4), .clk(in_2), .clr(in_3));  // open: en
  Register #(.width(1)) register_2 (.D(\输出电路_1_out_4 ), .Q(out_5), .clk(in_2), .clr(in_3));  // open: en

  // Other names for the same wires on the sheet: arrive = out_4; clk = in_2; hit = out_5; input[1:0] = in_1;
  //   reset = in_3
endmodule

// states
module \状态转移  (
  input  [1:0] in_1,
  input  [2:0] in_2,
  output [2:0] out_3
);

  wire and_1_out, and_2_out, and_3_out, and_4_out, and_5_out, and_6_out, and_7_out, and_8_out, and_9_out,
       and_10_out, and_11_out, and_12_out, and_13_out, and_14_out, and_15_out, and_16_out, and_17_out,
       and_18_out, not_1_out, not_2_out, not_3_out, not_4_out, not_5_out, not_6_out, not_7_out, not_8_out,
       not_9_out, not_10_out, not_11_out, not_12_out, not_13_out, not_14_out, not_15_out, not_16_out,
       not_17_out, not_18_out, not_19_out, not_20_out, not_21_out, not_22_out, not_23_out, not_24_out,
       not_25_out, not_26_out, not_27_out, not_28_out, not_29_out, not_30_out;

  not not_1 (not_1_out, in_2[0]);
  not not_2 (not_2_out, in_1[1]);
  not not_3 (not_3_out, in_1[0]);
  not not_4 (not_4_out, in_1[1]);
  not not_5 (not_5_out, in_1[1]);
  not not_6 (not_6_out, in_1[0]);
  not not_7 (not_7_out, in_2[2]);
  not not_8 (not_8_out, in_2[1]);
  not not_9 (not_9_out, in_1[1]);
  not not_10 (not_10_out, in_1[1]);
  not not_11 (not_11_out, in_1[0]);
  not not_12 (not_12_out, in_2[2]);
  not not_13 (not_13_out, in_2[0]);
  not not_14 (not_14_out, in_1[1]);
  not not_15 (not_15_out, in_2[2]);
  not not_16 (not_16_out, in_2[0]);
  not not_17 (not_17_out, in_1[0]);
  not not_18 (not_18_out, in_2[1]);
  not not_19 (not_19_out, in_1[0]);
  not not_20 (not_20_out, in_1[1]);
  not not_21 (not_21_out, in_1[0]);
  not not_22 (not_22_out, in_2[2]);
  not not_23 (not_23_out, in_2[1]);
  not not_24 (not_24_out, in_1[1]);
  not not_25 (not_25_out, in_1[0]);
  not not_26 (not_26_out, in_2[2]);
  not not_27 (not_27_out, in_2[2]);
  not not_28 (not_28_out, in_2[2]);
  not not_29 (not_29_out, in_1[0]);
  not not_30 (not_30_out, in_1[0]);
  and and_1 (and_1_out, in_2[1], not_1_out, not_2_out, not_3_out);
  and and_2 (and_2_out, in_2[1], in_2[0], not_4_out, in_1[0]);
  and and_3 (and_3_out, in_2[2], in_2[0], not_5_out, not_6_out);
  and and_4 (and_4_out, in_2[2], in_2[0], in_1[1], in_1[0]);
  and and_5 (and_5_out, in_2[2], in_2[1], in_1[0]);
  and and_6 (and_6_out, not_7_out, not_8_out, in_2[0], not_9_out);
  and and_7 (and_7_out, in_2[0], not_10_out, not_11_out);
  and and_8 (and_8_out, not_12_out, in_2[1], not_13_out, not_14_out, in_1[0]);
  and and_9 (and_9_out, not_15_out, in_2[1], not_16_out, in_1[1], not_17_out);
  and and_10 (and_10_out, in_2[1], in_2[0], in_1[1], in_1[0]);
  and and_11 (and_11_out, in_2[2], not_18_out, in_2[0], not_19_out);
  and and_12 (and_12_out, in_2[2], in_2[1], not_20_out, not_21_out);
  and and_13 (and_13_out, in_2[2], in_2[1], in_1[1], in_1[0]);
  and and_14 (and_14_out, not_22_out, not_23_out, not_24_out, not_25_out);
  and and_15 (and_15_out, not_26_out, in_2[0], in_1[1], in_1[0]);
  and and_16 (and_16_out, not_27_out, in_2[1], in_1[1], in_1[0]);
  and and_17 (and_17_out, not_28_out, in_2[1], in_2[0], not_29_out);
  and and_18 (and_18_out, in_2[2], in_2[1], in_1[1], not_30_out);
  or or_1 (out_3[2], and_1_out, and_2_out, and_3_out, and_4_out, and_5_out);
  or or_2 (out_3[1], and_6_out, and_7_out, and_8_out, and_9_out, and_10_out, and_11_out, and_12_out, and_13_out);
  or or_3 (out_3[0], and_14_out, and_15_out, and_16_out, and_17_out, and_18_out);

  // Other names for the same wires on the sheet: in_0 = in_1[0]; input[1:0] = in_1; in_1_t = in_1[1];
  //   next_state[2:0] = out_3; out_0 = out_3[0]; out_1 = out_3[1]; out_2 = out_3[2]; s0 = in_2[0]; state[2:0] = in_2;
  //   s1 = in_2[1]; s2 = in_2[2]
endmodule

// store
module \状态存储  (
  input  [2:0] in_1,
  input  in_2,
  input  in_3,
  output [2:0] out_4
);

  Register #(.width(1)) register_1 (.D(in_1[0]), .Q(out_4[0]), .clk(in_2), .clr(in_3));  // open: en
  Register #(.width(1)) register_2 (.D(in_1[1]), .Q(out_4[1]), .clk(in_2), .clr(in_3));  // open: en
  Register #(.width(1)) register_3 (.D(in_1[2]), .Q(out_4[2]), .clk(in_2), .clr(in_3));  // open: en

  // Other names for the same wires on the sheet: clk = in_2; out_0 = out_4[0]; output[2:0] = out_4; out_1 = out_4[1];
  //   out_2 = out_4[2]; reset = in_3; bit_0 = in_1[0]; state[2:0] = in_1; bit_1 = in_1[1]; bit_2 = in_1[2]
endmodule

// out
module \输出电路  (
  input  [1:0] in_1,
  input  [2:0] in_2,
  output out_3,
  output out_4
);

  wire and_1_out, and_2_out, and_3_out, and_4_out, and_5_out, and_6_out, and_7_out, and_8_out, not_1_out,
       not_2_out, not_3_out, not_4_out, not_5_out, not_6_out, not_7_out, not_8_out, not_9_out, not_10_out,
       not_11_out, not_12_out, not_13_out, not_14_out, not_15_out, not_16_out, not_17_out, not_18_out;

  not not_1 (not_1_out, in_2[0]);
  not not_2 (not_2_out, in_1[1]);
  not not_3 (not_3_out, in_1[0]);
  not not_4 (not_4_out, in_1[1]);
  not not_5 (not_5_out, in_2[1]);
  not not_6 (not_6_out, in_1[1]);
  not not_7 (not_7_out, in_1[0]);
  not not_8 (not_8_out, in_2[2]);
  not not_9 (not_9_out, in_2[0]);
  not not_10 (not_10_out, in_1[1]);
  not not_11 (not_11_out, in_2[2]);
  not not_12 (not_12_out, in_2[1]);
  not not_13 (not_13_out, in_2[0]);
  not not_14 (not_14_out, in_2[2]);
  not not_15 (not_15_out, in_2[0]);
  not not_16 (not_16_out, in_1[0]);
  not not_17 (not_17_out, in_1[1]);
  not not_18 (not_18_out, in_1[0]);
  and and_1 (and_1_out, in_2[1], not_1_out, not_2_out, not_3_out);
  and and_2 (and_2_out, in_2[1], in_2[0], not_4_out, in_1[0]);
  and and_3 (and_3_out, in_2[2], not_5_out, in_2[0], not_6_out, not_7_out);
  and and_4 (and_4_out, not_8_out, not_9_out, not_10_out, in_1[0]);
  and and_5 (and_5_out, not_11_out, not_12_out, not_13_out, in_1[1]);
  and and_6 (and_6_out, not_14_out, not_15_out, in_1[1], not_16_out);
  and and_7 (and_7_out, in_2[0], in_1[1], in_1[0]);
  and and_8 (and_8_out, in_2[1], in_2[0], not_17_out, not_18_out);
  or or_1 (out_3, and_1_out, and_2_out, and_3_out);
  or or_2 (out_4, and_4_out, and_5_out, and_6_out, and_7_out, and_8_out);

  // Other names for the same wires on the sheet: arrive = out_3; hit = out_4; in_0 = in_1[0]; input[1:0] = in_1;
  //   in_1_t = in_1[1]; s0 = in_2[0]; state[2:0] = in_2; s1 = in_2[1]; s2 = in_2[2]
endmodule

module temp (
  input  s2,
  input  s1,
  input  s0,
  input  in_1,
  input  in_0,
  output arrive,
  output hit
);

  wire and_1_out, and_2_out, and_3_out, and_4_out, and_5_out, and_6_out, and_7_out, and_8_out, not_1_out,
       not_2_out, not_3_out, not_4_out, not_5_out, not_6_out, not_7_out, not_8_out, not_9_out, not_10_out,
       not_11_out, not_12_out, not_13_out, not_14_out, not_15_out, not_16_out, not_17_out, not_18_out;

  not not_1 (not_1_out, s0);
  not not_2 (not_2_out, in_1);
  not not_3 (not_3_out, in_0);
  not not_4 (not_4_out, in_1);
  not not_5 (not_5_out, s1);
  not not_6 (not_6_out, in_1);
  not not_7 (not_7_out, in_0);
  not not_8 (not_8_out, s2);
  not not_9 (not_9_out, s0);
  not not_10 (not_10_out, in_1);
  not not_11 (not_11_out, s2);
  not not_12 (not_12_out, s1);
  not not_13 (not_13_out, s0);
  not not_14 (not_14_out, s2);
  not not_15 (not_15_out, s0);
  not not_16 (not_16_out, in_0);
  not not_17 (not_17_out, in_1);
  not not_18 (not_18_out, in_0);
  and and_1 (and_1_out, s1, not_1_out, not_2_out, not_3_out);
  and and_2 (and_2_out, s1, s0, not_4_out, in_0);
  and and_3 (and_3_out, s2, not_5_out, s0, not_6_out, not_7_out);
  and and_4 (and_4_out, not_8_out, not_9_out, not_10_out, in_0);
  and and_5 (and_5_out, not_11_out, not_12_out, not_13_out, in_1);
  and and_6 (and_6_out, not_14_out, not_15_out, in_1, not_16_out);
  and and_7 (and_7_out, s0, in_1, in_0);
  and and_8 (and_8_out, s1, s0, not_17_out, not_18_out);
  or or_1 (arrive, and_1_out, and_2_out, and_3_out);
  or or_2 (hit, and_4_out, and_5_out, and_6_out, and_7_out, and_8_out);
endmodule
