// Logisim project problem2.circ as structural Verilog
module main (
  input  [1:0] in_1,
  input  in_2,
  input  in_3,
  output [3:0] \output 
);

  wire [2:0] register_1_q, status_1_out_3;

  status status_1 (.in_1(register_1_q), .in_2(in_1), .out_3(status_1_out_3));
  Register #(.width(3)) register_1 (.D(status_1_out_3), .Q(register_1_q), .clk(in_2), .clr(in_3));  // open: en
  \output  output_1 (.in_1(register_1_q), .in_2(in_1), .out_3(\output ));

  // Other names for the same wires on the sheet: clk = in_2; input[1:0] = in_1; rst = in_3

  // Notes on the sheet:
  //   Mealy型状态机
  //   状态转移
  //   输出逻辑
endmodule

module status (
  input  [2:0] in_1,
  input  [1:0] in_2,
  output [2:0] out_3
);
endmodule

module \output  (
  input  [2:0] in_1,
  input  [1:0] in_2,
  output [3:0] out_3
);
endmodule
