// Logisim project problem3.circ as structural Verilog: 4 circuits, main circuit main
module main (
  input  [3:0] in_1,
  input  in_2,
  input  in_3,
  output [1:0] \output 
);

  wire [3:0] register_1_q, status_1_out_3;

  status status_1 (.in_1(register_1_q), .in_2(in_1), .out_3(status_1_out_3));
  Register #(.width(4)) register_1 (.D(status_1_out_3), .Q(register_1_q), .clk(in_2), .clr(in_3));  // open: en
  \output  output_1 (.in_1(register_1_q), .out_2(\output ));

  // Other names for the same wires on the sheet: clk = in_2; input[3:0] = in_1; rst = in_3

  // Notes on the sheet:
  //   Moore型状态机
  //   状态转移
  //   输出逻辑
endmodule

module status (
  input  [3:0] in_1,
  input  [3:0] in_2,
  output [3:0] out_3
);
endmodule

module \output  (
  input  [3:0] in_1,
  output [1:0] out_2
);
endmodule

module new_main (
  input  in_1,
  input  [3:0] in_2,
  input  in_3
);

  wire [3:0] state1, state2;

  // Probe on in_2
  // Probe on state2
  Register #(.width(4)) register_1 (.D(in_2), .Q(state2), .clk(in_1), .clr(in_3));  // open: en
  // Probe on state1
  Register #(.width(4)) register_2 (.D(state2), .Q(state1), .clk(in_1), .clr(in_3));  // open: en

  // Other names for the same wires on the sheet: clk = in_1; rst = in_3; state3[3:0] = in_2
endmodule
