// Logisim project hugo1.circ as structural Verilog: 2 circuits, main circuit main
module main (
  input  [7:0] in_1,
  input  [7:0] in_2,
  input  [7:0] in_3,
  input  [7:0] in_4,
  input  [7:0] in_5,
  output [7:0] out_6
);

  wire [2:0] adder_1_out, bitfinder_1_index;
  wire [4:0] or_1_out, res_1_out_2, res_2_out_2, res_3_out_2, res_4_out_2, res_5_out_2;
  wire [5:0] bit_extender_1_out;

  res res_1 (.in_1(in_1), .out_2(res_1_out_2));
  res res_2 (.in_1(in_2), .out_2(res_2_out_2));
  res res_3 (.in_1(in_3), .out_2(res_3_out_2));
  res res_4 (.in_1(in_4), .out_2(res_4_out_2));
  res res_5 (.in_1(in_5), .out_2(res_5_out_2));
  assign or_1_out = res_1_out_2 | res_2_out_2 | res_3_out_2 | res_4_out_2 | res_5_out_2;  // OR_Gate or_1, 5 bits wide
  // Probe on or_1_out
  assign bit_extender_1_out = {{1{1'b0}}, or_1_out};  // Bit_Extender bit_extender_1
  BitFinder #(.width(6), .\type ("low0")) bitfinder_1 (
    .in(bit_extender_1_out), .index(bitfinder_1_index));  // open: found
  // Probe on bitfinder_1_index
  Adder #(.width(3)) adder_1 (.a(bitfinder_1_index), .b(3'b001), .out(adder_1_out));  // open: cin, cout
  assign out_6 = {{5{1'b0}}, adder_1_out};  // Bit_Extender bit_extender_2
endmodule

module res (
  input  [7:0] in_1,
  output [4:0] out_2
);

  wire comparator_1_eq, comparator_2_eq, comparator_3_eq, comparator_4_eq, comparator_5_eq;
  wire [4:0] bit_extender_1_out, bit_extender_2_out, bit_extender_3_out, bit_extender_4_out,
       bit_extender_5_out, shifter_1_out, shifter_2_out, shifter_3_out, shifter_4_out, shifter_5_out;

  Comparator #(.mode("unsigned")) comparator_1 (.a(in_1), .b(8'h1), .eq(comparator_1_eq));  // open: gt, lt
  Comparator #(.mode("unsigned")) comparator_2 (.a(in_1), .b(8'h2), .eq(comparator_2_eq));  // open: gt, lt
  Comparator #(.mode("unsigned")) comparator_3 (.a(in_1), .b(8'h3), .eq(comparator_3_eq));  // open: gt, lt
  Comparator #(.mode("unsigned")) comparator_4 (.a(in_1), .b(8'h4), .eq(comparator_4_eq));  // open: gt, lt
  Comparator #(.mode("unsigned")) comparator_5 (.a(in_1), .b(8'h5), .eq(comparator_5_eq));  // open: gt, lt
  assign bit_extender_1_out = {{4{1'b0}}, comparator_1_eq};  // Bit_Extender bit_extender_1
  assign bit_extender_2_out = {{4{1'b0}}, comparator_2_eq};  // Bit_Extender bit_extender_2
  assign bit_extender_3_out = {{4{1'b0}}, comparator_3_eq};  // Bit_Extender bit_extender_3
  assign bit_extender_4_out = {{4{1'b0}}, comparator_4_eq};  // Bit_Extender bit_extender_4
  assign bit_extender_5_out = {{4{1'b0}}, comparator_5_eq};  // Bit_Extender bit_extender_5
  Shifter #(.width(5)) shifter_1 (.in(bit_extender_1_out), .\dist (3'b000), .out(shifter_1_out));
  Shifter #(.width(5)) shifter_2 (.in(bit_extender_2_out), .\dist (3'b001), .out(shifter_2_out));
  Shifter #(.width(5)) shifter_3 (.in(bit_extender_3_out), .\dist (3'b010), .out(shifter_3_out));
  Shifter #(.width(5)) shifter_4 (.in(bit_extender_4_out), .\dist (3'b011), .out(shifter_4_out));
  Shifter #(.width(5)) shifter_5 (.in(bit_extender_5_out), .\dist (3'b100), .out(shifter_5_out));
  ExactlyOne xor_1[4:0] (
    .out(out_2), .in0(shifter_1_out), .in1(shifter_2_out), .in2(shifter_3_out), .in3(shifter_4_out),
    .in4(shifter_5_out));

  // Other names for the same wires on the sheet: input_1[7:0] = in_1
endmodule
