// Logisim project hugo2.circ as structural Verilog
module main (
  input  [1:0] in_1,
  input  in_2,
  input  in_3,
  output [3:0] out_4
);

  wire clock_1_out, init;
  wire [2:0] register_1_q, status_1_out_3;
  wire [3:0] bit_extender_1_out;

  Counter #(.width(1), .max('h1), .ongoal("stay")) counter_1 (
    .Q(init), .clk(clock_1_out));  // open: load, D, count, carry, clr
  Clock clock_1 (.out(clock_1_out));
  status status_1 (.in_1(register_1_q), .in_2(in_1), .out_3(status_1_out_3));
  Register #(.width(3)) register_1 (.D(status_1_out_3), .Q(register_1_q), .clk(in_3), .clr(in_2));  // open: en
  assign bit_extender_1_out = {{1{1'b0}}, status_1_out_3};  // Bit_Extender bit_extender_1
  Adder #(.width(4)) adder_1 (.a(bit_extender_1_out), .b(4'b0001), .out(out_4));  // open: cin, cout

  // Other names for the same wires on the sheet: clk = in_3; rst = in_2
endmodule

module status (
  input  [2:0] in_1,
  input  [1:0] in_2,
  output [2:0] out_3
);

  wire and_1_out, and_2_out, and_3_out, and_4_out, and_5_out, and_6_out, and_7_out, and_8_out, and_9_out,
       and_10_out, and_11_out, and_12_out, and_13_out, and_14_out, and_15_out, and_16_out, and_17_out,
       and_18_out, and_19_out, and_20_out, not_1_out, not_2_out, not_3_out, not_4_out, not_5_out, not_6_out,
       not_7_out, not_8_out, not_9_out, not_10_out, not_11_out, not_12_out, not_13_out, not_14_out,
       not_15_out, not_16_out, not_17_out, not_18_out, not_19_out, not_20_out, not_21_out, not_22_out,
       not_23_out, not_24_out, not_25_out, not_26_out, not_27_out, not_28_out, not_29_out, not_30_out,
       not_31_out, not_32_out, not_33_out, not_34_out, not_35_out, not_36_out;

  not not_1 (not_1_out, in_1[1]);
  not not_2 (not_2_out, in_1[0]);
  not not_3 (not_3_out, in_2[0]);
  not not_4 (not_4_out, in_2[0]);
  not not_5 (not_5_out, in_2[1]);
  not not_6 (not_6_out, in_1[1]);
  not not_7 (not_7_out, in_1[0]);
  not not_8 (not_8_out, in_1[2]);
  not not_9 (not_9_out, in_1[0]);
  not not_10 (not_10_out, in_2[0]);
  not not_11 (not_11_out, in_1[2]);
  not not_12 (not_12_out, in_2[1]);
  not not_13 (not_13_out, in_1[2]);
  not not_14 (not_14_out, in_2[1]);
  not not_15 (not_15_out, in_1[0]);
  not not_16 (not_16_out, in_2[1]);
  not not_17 (not_17_out, in_2[0]);
  not not_18 (not_18_out, in_2[0]);
  not not_19 (not_19_out, in_1[2]);
  not not_20 (not_20_out, in_1[1]);
  not not_21 (not_21_out, in_1[0]);
  not not_22 (not_22_out, in_2[1]);
  not not_23 (not_23_out, in_1[2]);
  not not_24 (not_24_out, in_1[1]);
  not not_25 (not_25_out, in_2[0]);
  not not_26 (not_26_out, in_1[1]);
  not not_27 (not_27_out, in_1[2]);
  not not_28 (not_28_out, in_1[0]);
  not not_29 (not_29_out, in_2[0]);
  not not_30 (not_30_out, in_2[1]);
  not not_31 (not_31_out, in_1[1]);
  not not_32 (not_32_out, in_1[0]);
  not not_33 (not_33_out, in_2[1]);
  not not_34 (not_34_out, in_2[0]);
  not not_35 (not_35_out, in_1[1]);
  not not_36 (not_36_out, in_1[0]);
  and and_1 (and_1_out, not_1_out, not_2_out, in_2[1], not_3_out);
  and and_2 (and_2_out, in_1[1], in_1[0], in_2[1], not_4_out);
  and and_3 (and_3_out, in_1[2], not_5_out);
  and and_4 (and_4_out, in_1[2], not_6_out, in_1[0]);
  and and_5 (and_5_out, in_1[2], in_1[1], not_7_out);
  and and_6 (and_6_out, not_8_out, not_9_out, in_2[1], not_10_out);
  and and_7 (and_7_out, not_11_out, in_1[0], not_12_out, in_2[0]);
  and and_8 (and_8_out, not_13_out, in_1[1], in_2[0]);
  and and_9 (and_9_out, in_1[1], in_1[0], not_14_out);
  and and_10 (and_10_out, in_1[2], not_15_out, in_2[1], in_2[0]);
  and and_11 (and_11_out, in_1[2], in_1[0], not_16_out, not_17_out);
  and and_12 (and_12_out, in_1[2], in_1[1], not_18_out);
  and and_13 (and_13_out, not_19_out, not_20_out, not_21_out, not_22_out, in_2[0]);
  and and_14 (and_14_out, not_23_out, not_24_out, in_2[1], not_25_out);
  and and_15 (and_15_out, not_26_out, in_1[0], in_2[1]);
  and and_16 (and_16_out, not_27_out, in_1[1], not_28_out, not_29_out);
  and and_17 (and_17_out, in_1[1], in_1[0], not_30_out);
  and and_18 (and_18_out, in_1[2], not_31_out, not_32_out, not_33_out, not_34_out);
  and and_19 (and_19_out, in_1[2], not_35_out, in_2[1], in_2[0]);
  and and_20 (and_20_out, in_1[2], in_1[1], not_36_out, in_2[0]);
  or or_1 (out_3[2], and_1_out, and_2_out, and_3_out, and_4_out, and_5_out);
  or or_2 (out_3[1], and_6_out, and_7_out, and_8_out, and_9_out, and_10_out, and_11_out, and_12_out);
  or or_3 (out_3[0], and_13_out, and_14_out, and_15_out, and_16_out, and_17_out, and_18_out, and_19_out, and_20_out);
endmodule

module \output  (
  input  [2:0] in_1,
  input  [1:0] in_2,
  output [3:0] out_3
);
endmodule

module temp1 (
  input  s2,
  input  s1,
  input  s0,
  input  in1,
  input  in0,
  output out2,
  output out1,
  output out0
);

  wire and_1_out, and_2_out, and_3_out, and_4_out, and_5_out, and_6_out, and_7_out, and_8_out, and_9_out,
       and_10_out, and_11_out, and_12_out, and_13_out, and_14_out, and_15_out, and_16_out, and_17_out,
       and_18_out, and_19_out, and_20_out, not_1_out, not_2_out, not_3_out, not_4_out, not_5_out, not_6_out,
       not_7_out, not_8_out, not_9_out, not_10_out, not_11_out, not_12_out, not_13_out, not_14_out,
       not_15_out, not_16_out, not_17_out, not_18_out, not_19_out, not_20_out, not_21_out, not_22_out,
       not_23_out, not_24_out, not_25_out, not_26_out, not_27_out, not_28_out, not_29_out, not_30_out,
       not_31_out, not_32_out, not_33_out, not_34_out, not_35_out, not_36_out;

  not not_1 (not_1_out, s1);
  not not_2 (not_2_out, s0);
  not not_3 (not_3_out, in0);
  not not_4 (not_4_out, in0);
  not not_5 (not_5_out, in1);
  not not_6 (not_6_out, s1);
  not not_7 (not_7_out, s0);
  not not_8 (not_8_out, s2);
  not not_9 (not_9_out, s0);
  not not_10 (not_10_out, in0);
  not not_11 (not_11_out, s2);
  not not_12 (not_12_out, in1);
  not not_13 (not_13_out, s2);
  not not_14 (not_14_out, in1);
  not not_15 (not_15_out, s0);
  not not_16 (not_16_out, in1);
  not not_17 (not_17_out, in0);
  not not_18 (not_18_out, in0);
  not not_19 (not_19_out, s2);
  not not_20 (not_20_out, s1);
  not not_21 (not_21_out, s0);
  not not_22 (not_22_out, in1);
  not not_23 (not_23_out, s2);
  not not_24 (not_24_out, s1);
  not not_25 (not_25_out, in0);
  not not_26 (not_26_out, s1);
  not not_27 (not_27_out, s2);
  not not_28 (not_28_out, s0);
  not not_29 (not_29_out, in0);
  not not_30 (not_30_out, in1);
  not not_31 (not_31_out, s1);
  not not_32 (not_32_out, s0);
  not not_33 (not_33_out, in1);
  not not_34 (not_34_out, in0);
  not not_35 (not_35_out, s1);
  not not_36 (not_36_out, s0);
  and and_1 (and_1_out, not_1_out, not_2_out, in1, not_3_out);
  and and_2 (and_2_out, s1, s0, in1, not_4_out);
  and and_3 (and_3_out, s2, not_5_out);
  and and_4 (and_4_out, s2, not_6_out, s0);
  and and_5 (and_5_out, s2, s1, not_7_out);
  and and_6 (and_6_out, not_8_out, not_9_out, in1, not_10_out);
  and and_7 (and_7_out, not_11_out, s0, not_12_out, in0);
  and and_8 (and_8_out, not_13_out, s1, in0);
  and and_9 (and_9_out, s1, s0, not_14_out);
  and and_10 (and_10_out, s2, not_15_out, in1, in0);
  and and_11 (and_11_out, s2, s0, not_16_out, not_17_out);
  and and_12 (and_12_out, s2, s1, not_18_out);
  and and_13 (and_13_out, not_19_out, not_20_out, not_21_out, not_22_out, in0);
  and and_14 (and_14_out, not_23_out, not_24_out, in1, not_25_out);
  and and_15 (and_15_out, not_26_out, s0, in1);
  and and_16 (and_16_out, not_27_out, s1, not_28_out, not_29_out);
  and and_17 (and_17_out, s1, s0, not_30_out);
  and and_18 (and_18_out, s2, not_31_out, not_32_out, not_33_out, not_34_out);
  and and_19 (and_19_out, s2, not_35_out, in1, in0);
  and and_20 (and_20_out, s2, s1, not_36_out, in0);
  or or_1 (out2, and_1_out, and_2_out, and_3_out, and_4_out, and_5_out);
  or or_2 (out1, and_6_out, and_7_out, and_8_out, and_9_out, and_10_out, and_11_out, and_12_out);
  or or_3 (out0, and_13_out, and_14_out, and_15_out, and_16_out, and_17_out, and_18_out, and_19_out, and_20_out);
endmodule
