// Logisim project CPU-单周期.circ as structural Verilog: 11 circuits, main circuit main
module GRF (
  input  in_1,
  input  in_2,
  input  in_3,
  input  [4:0] in_4,
  input  [4:0] in_5,
  input  [4:0] in_6,
  input  [31:0] in_7,
  output [31:0] out_8,
  output [31:0] out_9
);

  wire en_0, en_1, en_2, en_3, en_4, en_5, en_6, en_7, en_8, en_9, en_10, en_11, en_12, en_13, en_14, en_15,
       en_16, en_17, en_18, en_19, en_20, en_21, en_22, en_23, en_24, en_25, en_26, en_27, en_28, en_29,
       en_30, en_31, multiplexer_1_out;
  wire [31:0] Out_0, Out_1, Out_2, Out_3, Out_4, Out_5, Out_6, Out_7, Out_8_t, Out_9_t, Out_10, Out_11,
       Out_12, Out_13, Out_14, Out_15, Out_16, Out_17, Out_18, Out_19, Out_20, Out_21, Out_22, Out_23,
       Out_24, Out_25, Out_26, Out_27, Out_28, Out_29, Out_30, Out_31;

  Demultiplexer #(.select(5)) demultiplexer_1 (
    .out0(en_0), .out1(en_1), .out2(en_2), .out3(en_3), .out4(en_4), .out5(en_5), .out6(en_6), .out7(en_7),
    .out8(en_8), .out9(en_9), .out10(en_10), .out11(en_11), .out12(en_12), .out13(en_13), .out14(en_14),
    .out15(en_15), .out16(en_16), .out17(en_17), .out18(en_18), .out19(en_19), .out20(en_20), .out21(en_21),
    .out22(en_22), .out23(en_23), .out24(en_24), .out25(en_25), .out26(en_26), .out27(en_27), .out28(en_28),
    .out29(en_29), .out30(en_30), .out31(en_31), .in(multiplexer_1_out), .sel(in_6));  // open: en
  Multiplexer multiplexer_1 (.in0(1'b0), .in1(1'b1), .out(multiplexer_1_out), .sel(in_3));  // open: en
  Multiplexer #(.select(5), .width(32)) multiplexer_2 (
    .in0(Out_0), .in1(Out_1), .in2(Out_2), .in3(Out_3), .in4(Out_4), .in5(Out_5), .in6(Out_6), .in7(Out_7),
    .in8(Out_8_t), .in9(Out_9_t), .in10(Out_10), .in11(Out_11), .in12(Out_12), .in13(Out_13), .in14(Out_14),
    .in15(Out_15), .in16(Out_16), .in17(Out_17), .in18(Out_18), .in19(Out_19), .in20(Out_20), .in21(Out_21),
    .in22(Out_22), .in23(Out_23), .in24(Out_24), .in25(Out_25), .in26(Out_26), .in27(Out_27), .in28(Out_28),
    .in29(Out_29), .in30(Out_30), .in31(Out_31), .out(out_8), .sel(in_4));  // open: en
  Multiplexer #(.select(5), .width(32)) multiplexer_3 (
    .in0(Out_0), .in1(Out_1), .in2(Out_2), .in3(Out_3), .in4(Out_4), .in5(Out_5), .in6(Out_6), .in7(Out_7),
    .in8(Out_8_t), .in9(Out_9_t), .in10(Out_10), .in11(Out_11), .in12(Out_12), .in13(Out_13), .in14(Out_14),
    .in15(Out_15), .in16(Out_16), .in17(Out_17), .in18(Out_18), .in19(Out_19), .in20(Out_20), .in21(Out_21),
    .in22(Out_22), .in23(Out_23), .in24(Out_24), .in25(Out_25), .in26(Out_26), .in27(Out_27), .in28(Out_28),
    .in29(Out_29), .in30(Out_30), .in31(Out_31), .out(out_9), .sel(in_5));  // open: en
  Register #(.width(32)) register_1 (.D(in_7), .en(1'b0), .Q(Out_0), .clk(in_1), .clr(in_2));
  Register #(.width(32)) register_2 (.D(in_7), .en(en_4), .Q(Out_4), .clk(in_1), .clr(in_2));
  Register #(.width(32)) register_3 (.D(in_7), .en(en_8), .Q(Out_8_t), .clk(in_1), .clr(in_2));
  Register #(.width(32)) register_4 (.D(in_7), .en(en_12), .Q(Out_12), .clk(in_1), .clr(in_2));
  Register #(.width(32)) register_5 (.D(in_7), .en(en_16), .Q(Out_16), .clk(in_1), .clr(in_2));
  Register #(.width(32)) register_6 (.D(in_7), .en(en_20), .Q(Out_20), .clk(in_1), .clr(in_2));
  Register #(.width(32)) register_7 (.D(in_7), .en(en_24), .Q(Out_24), .clk(in_1), .clr(in_2));
  Register #(.width(32)) register_8 (.D(in_7), .en(en_28), .Q(Out_28), .clk(in_1), .clr(in_2));
  Register #(.width(32)) register_9 (.D(in_7), .en(en_1), .Q(Out_1), .clk(in_1), .clr(in_2));
  Register #(.width(32)) register_10 (.D(in_7), .en(en_5), .Q(Out_5), .clk(in_1), .clr(in_2));
  Register #(.width(32)) register_11 (.D(in_7), .en(en_9), .Q(Out_9_t), .clk(in_1), .clr(in_2));
  Register #(.width(32)) register_12 (.D(in_7), .en(en_13), .Q(Out_13), .clk(in_1), .clr(in_2));
  Register #(.width(32)) register_13 (.D(in_7), .en(en_17), .Q(Out_17), .clk(in_1), .clr(in_2));
  Register #(.width(32)) register_14 (.D(in_7), .en(en_21), .Q(Out_21), .clk(in_1), .clr(in_2));
  Register #(.width(32)) register_15 (.D(in_7), .en(en_25), .Q(Out_25), .clk(in_1), .clr(in_2));
  Register #(.width(32)) register_16 (.D(in_7), .en(en_29), .Q(Out_29), .clk(in_1), .clr(in_2));
  Register #(.width(32)) register_17 (.D(in_7), .en(en_2), .Q(Out_2), .clk(in_1), .clr(in_2));
  Register #(.width(32)) register_18 (.D(in_7), .en(en_6), .Q(Out_6), .clk(in_1), .clr(in_2));
  Register #(.width(32)) register_19 (.D(in_7), .en(en_10), .Q(Out_10), .clk(in_1), .clr(in_2));
  Register #(.width(32)) register_20 (.D(in_7), .en(en_14), .Q(Out_14), .clk(in_1), .clr(in_2));
  Register #(.width(32)) register_21 (.D(in_7), .en(en_18), .Q(Out_18), .clk(in_1), .clr(in_2));
  Register #(.width(32)) register_22 (.D(in_7), .en(en_22), .Q(Out_22), .clk(in_1), .clr(in_2));
  Register #(.width(32)) register_23 (.D(in_7), .en(en_26), .Q(Out_26), .clk(in_1), .clr(in_2));
  Register #(.width(32)) register_24 (.D(in_7), .en(en_30), .Q(Out_30), .clk(in_1), .clr(in_2));
  Register #(.width(32)) register_25 (.D(in_7), .en(en_3), .Q(Out_3), .clk(in_1), .clr(in_2));
  Register #(.width(32)) register_26 (.D(in_7), .en(en_7), .Q(Out_7), .clk(in_1), .clr(in_2));
  Register #(.width(32)) register_27 (.D(in_7), .en(en_11), .Q(Out_11), .clk(in_1), .clr(in_2));
  Register #(.width(32)) register_28 (.D(in_7), .en(en_15), .Q(Out_15), .clk(in_1), .clr(in_2));
  Register #(.width(32)) register_29 (.D(in_7), .en(en_19), .Q(Out_19), .clk(in_1), .clr(in_2));
  Register #(.width(32)) register_30 (.D(in_7), .en(en_23), .Q(Out_23), .clk(in_1), .clr(in_2));
  Register #(.width(32)) register_31 (.D(in_7), .en(en_27), .Q(Out_27), .clk(in_1), .clr(in_2));
  Register #(.width(32)) register_32 (.D(in_7), .en(en_31), .Q(Out_31), .clk(in_1), .clr(in_2));

  // Other names for the same wires on the sheet: A1[4:0] = in_4; A2[4:0] = in_5; A3[4:0] = in_6; clk = in_1;
  //   RD1[31:0] = out_8; RD2[31:0] = out_9; rst = in_2; In[31:0] = in_7; WD[31:0] = in_7; WE = in_3

  // Notes on the sheet:
  //   Input
  //   Output
  //   0号寄存器恒为0
  //   寄存器组
endmodule

// 32
module main (
  input  in_1,
  output [31:0] out_2,
  output out_3,
  output [31:0] out_4,
  output [31:0] out_5,
  output out_6,
  output [31:0] out_7,
  output [4:0] out_8,
  output [31:0] out_9
);

  wire ALUSrc, Branch, CLK, Equals, FlowJudge, JR, JUMP, ld, link, MemtoReg, OverFlow, sll, Stop,
       UnsignedExt, WriteReg;
  wire [3:0] ALUOp;
  wire [4:0] cu_shamt, multiplexer_1_out, Shamt;
  wire [31:0] dm_1_rd, multiplexer_4_out, multiplexer_6_out, npc_1_next_pc, Offset, PC_4, Ra;

  Clock clock_1 (.out(CLK));
  // Probe on out_2
  // Probe on PC_4
  // Probe on out_5
  IFU ifu_1 (.in_1(npc_1_next_pc), .in_2(CLK), .in_3(in_1), .in_4(Stop), .out_5(out_5), .out_6(out_2));
  NPC npc_1 (
    .PC(out_5), .Next_PC(npc_1_next_pc), .Branch(Branch), .Equals(Equals), .PC_4(PC_4), .in_4(Offset),
    .Ins_26(out_2[25:0]), .in_6(JR), .in_7(JUMP), .Ra(Ra));
  CU cu_1 (
    .Opcode(out_2[31:26]), .func(out_2[5:0]), .out_4(FlowJudge), .out_5(JR), .out_6(JUMP), .out_7(out_6),
    .out_8(ALUSrc), .out_9(out_3), .out_10(ld), .out_11(WriteReg), .out_12(UnsignedExt), .out_13(MemtoReg),
    .out_14(Branch), .out_15(cu_shamt), .ALUOp(ALUOp), .out_3(Stop), .out_16(sll), .out_17(link));
  Multiplexer #(.width(5)) multiplexer_1 (
    .in0(out_2[20:16]), .in1(out_2[15:11]), .out(multiplexer_1_out), .sel(WriteReg));  // open: en
  GRF grf_1 (
    .in_1(CLK), .in_2(in_1), .in_3(out_6), .in_4(out_2[25:21]), .in_5(out_2[20:16]), .in_6(out_8),
    .in_7(multiplexer_6_out), .out_8(Ra), .out_9(out_7));
  Multiplexer #(.width(5)) multiplexer_2 (
    .in0(multiplexer_1_out), .in1({5{1'b1}}), .out(out_8), .sel(link));  // open: en
  EXT SignedImm (.in_1(UnsignedExt), .Imm_16(out_2[15:0]), .Imm_32(Offset));
  Multiplexer #(.width(5)) multiplexer_3 (.in0(cu_shamt), .in1(out_2[10:6]), .out(Shamt), .sel(sll));  // open: en
  Multiplexer #(.width(32)) multiplexer_4 (
    .in0(out_7), .in1(Offset), .out(multiplexer_4_out), .sel(ALUSrc));  // open: en
  ALU u_OverFlow (
    .A(Ra), .B(multiplexer_4_out), .Shamt(Shamt), .Equals(Equals), .ALUResult(out_4), .AluOp(ALUOp),
    .FlowJudge(FlowJudge), .OverFlow(OverFlow));
  DM dm_1 (.Addr(out_4), .WD(out_7), .RD(dm_1_rd), .in_1(CLK), .in_2(out_3), .in_3(ld), .in_4(in_1));
  Multiplexer #(.width(32)) multiplexer_5 (.in0(out_4), .in1(dm_1_rd), .out(out_9), .sel(MemtoReg));  // open: en
  Multiplexer #(.width(32)) multiplexer_6 (.in0(out_9), .in1(PC_4), .out(multiplexer_6_out), .sel(link));  // open: en

  // Other names for the same wires on the sheet: Instr[31:0] = out_2; Instr_26[25:0] = out_2[25:0];
  //   sa[4:0] = out_2[10:6]; MemAddr[31:0] = out_4; MemWrite = out_3; pc[31:0] = out_5; rd[4:0] = out_8;
  //   RegData[31:0] = out_9; RegWrite = out_6; Reset = in_1; WriteData[31:0] = out_7

  // Notes on the sheet:
  //   Input
  //   rs/base
  //   rt
  //   offset
  //   Output
  //   Debug
endmodule

module PC (
  input  in_1,
  input  in_2,
  input  in_3,
  input  [31:0] PC_prime,
  output [31:0] PC
);

  wire Stop;
  wire [31:0] register_1_q, subtractor_1_out;

  or or_1 (Stop, in_1, 1'b1);
  Subtractor #(.width(32)) subtractor_1 (.a(PC_prime), .b(32'h3000), .out(subtractor_1_out));  // open: bin, bout
  Register #(.width(32)) register_1 (.D(subtractor_1_out), .en(Stop), .Q(register_1_q), .clk(in_2), .clr(in_3));
  // Probe on PC
  // Probe on PC_prime
  Adder #(.width(32)) adder_1 (.a(register_1_q), .b(32'h3000), .out(PC));  // open: cin, cout

  // Other names for the same wires on the sheet: CLK = in_2; RST = in_3

  // Notes on the sheet:
  //   Input
  //   Debug
endmodule

module IM (
  input  [31:0] PC,
  output [31:0] Instr
);

  wire [11:0] addr;
  wire [31:0] subtractor_1_out;

  // Probe on addr
  Subtractor #(.width(32)) subtractor_1 (
    .a(PC), .b(32'h3000), .out({subtractor_1_out[31:14], addr, subtractor_1_out[1:0]}));  // open: bin, bout
  ROM #(.addrWidth(12), .dataWidth(32)) rom_1 (.addr(addr), .data(Instr));  // open: sel

  // Notes on the sheet:
  //   Debug
  //   contents of rom_1 (hex, n*v repeats v):
  //   0 0 341c0000 341d0000 0 c000c06 3e00008 341c0000 341d0000 34013456 210820 8c010004 ac010004 3c027878
  //   411822 3c051234 34040005 0 3401ffff 240821 ac250000 3401ffff 240821 8c230000 10650001 1000000d
  //   34670404 10e3000b 0 3c087777 3508ffff 80022 34001100 e65020 34080000 34090001 340a0001 10a4020
  //   1109fffe 1000ffff
endmodule

module DM (
  input  in_1,
  input  in_2,
  input  in_3,
  input  in_4,
  input  [31:0] Addr,
  input  [31:0] WD,
  output [31:0] RD
);

  Decoder #(.select(2), .enable("false")) decoder_1 (.sel(Addr[1:0]));  // open: out0, out1, out2, out3
  // Probe on Addr[13:2]
  // Probe on RD
  // Probe on WD
  RAM #(.addrWidth(12), .dataWidth(32), .bus("separate")) ram_1 (
    .addr(Addr[13:2]), .din(WD), .data(RD), .str(in_2), .clk(in_1), .ld(in_3), .clr(in_4));  // open: sel

  // Other names for the same wires on the sheet: byte[1:0] = Addr[1:0]; Addr_t[11:0] = Addr[13:2]; CLK = in_1;
  //   ld = in_3; Reset = in_4; WD_byte[7:0] = WD[7:0]; WD_half[15:0] = WD[15:0]; WE = in_2

  // Notes on the sheet:
  //   Input
  //   Debug
endmodule

module ALU (
  input  [31:0] A,
  input  [31:0] B,
  input  [4:0] Shamt,
  input  [3:0] AluOp,
  input  FlowJudge,
  output Equals,
  output [31:0] ALUResult,
  output OverFlow
);

  wire comparator_1_eq, comparator_2_lt, comparator_3_lt, comparator_4_gt, comparator_5_gt, OverFlow_t;
  wire [31:0] adder_1_out, and_1_out, bit_extender_1_out, bit_extender_2_out, bit_extender_3_out,
       bit_extender_4_out, bit_extender_5_out, divider_1_out, multiplier_1_out, nor_1_out, or_1_out,
       shifter_1_out, shifter_2_out, shifter_3_out, subtractor_1_out, xor_1_out;

  assign and_1_out = A & B;  // AND_Gate and_1, 32 bits wide
  assign or_1_out = A | B;  // OR_Gate or_1, 32 bits wide
  Adder #(.width(32)) adder_1 (.a(A), .b(B), .out(adder_1_out), .cout(OverFlow_t));  // open: cin
  Subtractor #(.width(32)) subtractor_1 (.a(A), .b(B), .out(subtractor_1_out), .bout(OverFlow_t));  // open: bin
  Multiplier #(.width(32)) multiplier_1 (.a(A), .b(B), .out(multiplier_1_out));  // open: cin, cout
  Divider #(.width(32)) divider_1 (.a(A), .b(B), .out(divider_1_out));  // open: upper, rem
  assign xor_1_out = A ^ B;  // XOR_Gate xor_1, 32 bits wide
  assign nor_1_out = ~(A | B);  // NOR_Gate nor_1, 32 bits wide
  Shifter #(.width(32)) shifter_1 (.in(B), .\dist (Shamt), .out(shifter_1_out));
  Shifter #(.width(32), .shift("lr")) shifter_2 (.in(B), .\dist (Shamt), .out(shifter_2_out));
  Shifter #(.width(32), .shift("ar")) shifter_3 (.in(B), .\dist (Shamt), .out(shifter_3_out));
  Comparator #(.width(32)) comparator_1 (.a(A), .b(B), .eq(comparator_1_eq));  // open: gt, lt
  Comparator #(.width(32)) comparator_2 (.a(A), .b(B), .lt(comparator_2_lt));  // open: gt, eq
  Comparator #(.width(32), .mode("unsigned")) comparator_3 (.a(A), .b(B), .lt(comparator_3_lt));  // open: gt, eq
  Comparator #(.width(32)) comparator_4 (.a(A), .b(B), .gt(comparator_4_gt));  // open: eq, lt
  Comparator #(.width(32), .mode("unsigned")) comparator_5 (.a(A), .b(B), .gt(comparator_5_gt));  // open: eq, lt
  assign bit_extender_1_out = {{31{1'b0}}, comparator_1_eq};  // Bit_Extender bit_extender_1
  assign bit_extender_2_out = {{31{1'b0}}, comparator_2_lt};  // Bit_Extender bit_extender_2
  assign bit_extender_3_out = {{31{1'b0}}, comparator_3_lt};  // Bit_Extender bit_extender_3
  assign bit_extender_4_out = {{31{1'b0}}, comparator_4_gt};  // Bit_Extender bit_extender_4
  assign bit_extender_5_out = {{31{1'b0}}, comparator_5_gt};  // Bit_Extender bit_extender_5
  Multiplexer #(.select(4), .width(32)) multiplexer_1 (
    .in0(adder_1_out), .in1(subtractor_1_out), .in2(multiplier_1_out), .in3(divider_1_out), .in4(and_1_out),
    .in5(or_1_out), .in6(xor_1_out), .in7(nor_1_out), .in8(shifter_1_out), .in9(shifter_2_out),
    .in10(shifter_3_out), .in11(bit_extender_1_out), .in12(bit_extender_2_out), .in13(bit_extender_3_out),
    .in14(bit_extender_4_out), .in15(bit_extender_5_out), .out(ALUResult), .sel(AluOp));  // open: en
  Comparator #(.width(32)) comparator_6 (.a(A), .b(B), .eq(Equals));  // open: gt, lt
  and and_2 (OverFlow, OverFlow_t, FlowJudge);
endmodule

module EXT (
  input  in_1,
  input  [15:0] Imm_16,
  output [31:0] Imm_32
);

  wire [31:0] bit_extender_1_out, bit_extender_2_out;

  assign bit_extender_1_out = {{16{Imm_16[15]}}, Imm_16};  // Bit_Extender bit_extender_1
  assign bit_extender_2_out = {{16{1'b0}}, Imm_16};  // Bit_Extender bit_extender_2
  Multiplexer #(.width(32)) multiplexer_1 (
    .in0(bit_extender_1_out), .in1(bit_extender_2_out), .out(Imm_32), .sel(in_1));  // open: en

  // Other names for the same wires on the sheet: UnsignedExt = in_1

  // Notes on the sheet:
  //    符号拓展
  //   0拓展
endmodule

module NPC (
  input  [31:0] PC,
  input  Branch,
  input  Equals,
  input  [31:0] in_4,
  input  [25:0] Ins_26,
  input  in_6,
  input  in_7,
  input  [31:0] Ra,
  output [31:0] Next_PC,
  output [31:0] PC_4
);

  wire If_Branch, Sequencial_next_pc;
  wire [1:0] priority_encoder_1_out;
  wire [31:0] PCBranch, shifter_1_out;

  Adder #(.width(32)) adder_1 (.a(PC), .b(32'h4), .out(PC_4));  // open: cin, cout
  Shifter #(.width(32)) shifter_1 (.in(in_4), .\dist (5'b00010), .out(shifter_1_out));
  Priority_Encoder #(.select(2)) priority_encoder_1 (
    .in0(Sequencial_next_pc), .in1(If_Branch), .in2(in_7), .in3(in_6), .out(priority_encoder_1_out));  // open: gs, en_out, en_in
  Multiplexer #(.select(2), .width(32)) multiplexer_1 (
    .in0(PC_4), .in1(PCBranch), .in2({PC[31:28], Ins_26, 2'b00}), .in3(Ra), .out(Next_PC),
    .sel(priority_encoder_1_out));  // open: en
  Adder #(.width(32)) adder_2 (.a(PC_4), .b(shifter_1_out), .out(PCBranch));  // open: cin, cout
  nor nor_1 (Sequencial_next_pc, If_Branch, in_6, in_7);
  and and_1 (If_Branch, Branch, Equals);
  // Probe on PC_4
  // Probe on PC
  // Probe on Next_PC

  // Other names for the same wires on the sheet: JR = in_6; JUMP = in_7; Offset[31:0] = in_4; PCJR[31:0] = Ra;
  //   PCJump[31:2] = {PC[31:28], Ins_26}

  // Notes on the sheet:
  //   Input
  //   Output
  //   Debug
endmodule

module IFU (
  input  [31:0] in_1,
  input  in_2,
  input  in_3,
  input  in_4,
  output [31:0] out_5,
  output [31:0] out_6
);

  PC pc_1 (.PC_prime(in_1), .PC(out_5), .in_2(in_2), .in_3(in_3), .in_1(in_4));
  IM im_1 (.PC(out_5), .Instr(out_6));
  // Probe on out_5
  // Probe on in_1

  // Other names for the same wires on the sheet: CLK = in_2; Instr[31:0] = out_6; PC[31:0] = out_5;
  //   PC_prime[31:0] = in_1; Reset = in_3; Stop = in_4

  // Notes on the sheet:
  //   Input
  //   Output
endmodule

module CU (
  input  [5:0] Opcode,
  input  [5:0] func,
  output out_3,
  output out_4,
  output out_5,
  output out_6,
  output out_7,
  output out_8,
  output out_9,
  output out_10,
  output out_11,
  output out_12,
  output out_13,
  output out_14,
  output [4:0] out_15,
  output out_16,
  output out_17,
  output [3:0] ALUOp
);

  wire add, and_10_out, and_12_out, and_14_out, and_16_out, and_18_out, beq, j, jal, jalr, jr_t, lui, lw,
       ori, R_Op, sub, sw;
  wire [4:0] multiplexer_1_out;
  wire [23:3] not_5_out;
  wire [29:9] not_12_out;

  not not_1 (not_5_out[23], Opcode[5]);
  not not_2 (not_5_out[19], Opcode[4]);
  or or_1 (out_5, jr_t, jalr);
  not not_3 (not_5_out[11], Opcode[2]);
  not not_4 (not_5_out[15], Opcode[3]);
  or or_2 (out_6, j, jal);
  not not_5 (not_5_out[3], Opcode[0]);
  not not_6 (not_5_out[7], Opcode[1]);
  or or_3 (out_17, jal, jalr);
  or or_4 (out_7, lw, ori, lui, out_16, add, sub);
  Multiplexer #(.width(5)) multiplexer_1 (
    .in0({5{1'b0}}), .in1(5'b10000), .out(multiplexer_1_out), .sel(lui));  // open: en
  and and_1 (R_Op, not_5_out[23], not_5_out[19], not_5_out[15], not_5_out[11], not_5_out[7], not_5_out[3]);
  and and_2 (ori, not_5_out[23], not_5_out[19], Opcode[3], Opcode[2], not_5_out[7], Opcode[0]);
  and and_3 (lw, Opcode[5], not_5_out[19], not_5_out[15], not_5_out[11], Opcode[1], Opcode[0]);
  and and_4 (sw, Opcode[5], not_5_out[19], Opcode[3], not_5_out[11], Opcode[1], Opcode[0]);
  and and_5 (beq, not_5_out[23], not_5_out[19], not_5_out[15], Opcode[2], not_5_out[7], not_5_out[3]);
  and and_6 (lui, not_5_out[23], not_5_out[19], Opcode[3], Opcode[2], Opcode[1], Opcode[0]);
  and and_7 (j, not_5_out[23], not_5_out[19], not_5_out[15], not_5_out[11], Opcode[1], not_5_out[3]);
  and and_8 (jal, not_5_out[23], not_5_out[19], not_5_out[15], not_5_out[11], Opcode[1], Opcode[0]);
  Multiplexer #(.width(5)) multiplexer_2 (
    .in0(multiplexer_1_out), .in1(5'b00010), .out(out_15), .sel(beq));  // open: en
  or or_5 (out_8, lw, sw, ori, lui);
  not not_7 (not_12_out[29], func[5]);
  buf or_6 (out_9, sw);  // OR_Gate
  not not_8 (not_12_out[21], func[3]);
  not not_9 (not_12_out[25], func[4]);
  buf or_7 (out_10, lw);  // OR_Gate
  not not_10 (not_12_out[17], func[2]);
  not not_11 (not_12_out[13], func[1]);
  or or_8 (out_11, out_16, add, sub);
  not not_12 (not_12_out[9], func[0]);
  buf or_9 (out_12, ori);  // OR_Gate
  or or_10 (out_13, lw, sw);
  or or_11 (ALUOp[0], beq, 1'b0, sub, 1'b0, 1'b0, 1'b0, 1'b0, ori, sub);
  or or_12 (ALUOp[1], 1'b0, 1'b0, 1'b0, 1'b0, 1'b0);
  or or_13 (ALUOp[2], 1'b0, 1'b0, 1'b0, 1'b0, ori);
  or or_14 (ALUOp[3], out_16, 1'b0, 1'b0, 1'b0, 1'b0, lui);
  and and_9 (out_16, R_Op, and_10_out);
  and and_10 (and_10_out, not_12_out[29], not_12_out[25], not_12_out[21], not_12_out[17], not_12_out[13], not_12_out[9]);
  and and_11 (add, R_Op, and_12_out);
  and and_12 (and_12_out, func[5], not_12_out[25], not_12_out[21], not_12_out[17], not_12_out[13], not_12_out[9]);
  and and_13 (sub, R_Op, and_14_out);
  and and_14 (and_14_out, func[5], not_12_out[25], not_12_out[21], not_12_out[17], func[1], not_12_out[9]);
  and and_15 (jr_t, R_Op, and_16_out);
  and and_16 (and_16_out, not_12_out[29], not_12_out[25], func[3], not_12_out[17], not_12_out[13], not_12_out[9]);
  and and_17 (jalr, R_Op, and_18_out);
  and and_18 (and_18_out, not_12_out[29], not_12_out[25], func[3], not_12_out[17], not_12_out[13], func[0]);
  buf or_15 (out_14, beq);  // OR_Gate

  assign out_3 = 1'b1;
  assign out_4 = 1'b0;

  // Other names for the same wires on the sheet: sll = out_16; ALUSrc = out_8; Branch = out_14; JR = out_5;
  //   JUMP = out_6; ld = out_10; link = out_17; MemtoReg = out_13; MemWrite = out_9; RegWrite = out_7;
  //   shamt[4:0] = out_15; UnsignedExt = out_12; WriteReg = out_11

  // Notes on the sheet:
  //   Output
endmodule

module test (
  input  [31:0] in_1,
  input  in_2,
  input  in_3,
  input  in_4,
  output [31:0] out_5
);

  Register #(.width(32)) register_1 (.D(in_1), .en(in_2), .Q(out_5), .clk(in_3), .clr(in_4));

  // Other names for the same wires on the sheet: clk = in_3; en_1 = in_2; In[31:0] = in_1; Out_1[31:0] = out_5;
  //   rst = in_4
endmodule
